// Logisim project 4Bit_Counter.circ as structural Verilog: 1 circuit, main circuit Bit4_Counter
module Bit4_Counter (
  input  Reset,
  output A0,
  output A1,
  output A2,
  output A3
);

  wire CP_out;

  Clock CP (.out(CP_out));
  // Master_Slave_Flip_Flop master_slave_flip_flop_1: pin names not known; wires that end beside it: 1'b1, 1'b1, CP_out, Reset, A0
  // Master_Slave_Flip_Flop master_slave_flip_flop_2: pin names not known; wires that end beside it: 1'b1, 1'b1, A0, Reset, A1
  // Master_Slave_Flip_Flop master_slave_flip_flop_3: pin names not known; wires that end beside it: 1'b1, 1'b1, A1, Reset, A2
  // Master_Slave_Flip_Flop master_slave_flip_flop_4: pin names not known; wires that end beside it: 1'b1, 1'b1, A2, Reset, A3
endmodule
