// Logisim project Master_Slave_JK_Flip_Flop.circ as structural Verilog: 1 circuit, main circuit Master_Slave_Flip_Flop
module Master_Slave_Flip_Flop (
  input  J,
  input  CP,
  input  K,
  output Q,
  output QBar
);

  wire nand_1_out, nand_2_out, nand_3_out, nand_4_out, nand_5_out, nand_6_out, nand_7_out, not_1_out,
       por_1_out;

  POR por_1 (.out(por_1_out));
  nand nand_1 (nand_1_out, QBar, J, CP);
  nand nand_2 (nand_2_out, CP, K, Q);
  not not_1 (not_1_out, por_1_out);
  nand nand_3 (nand_3_out, CP, CP);
  nand nand_4 (nand_4_out, nand_1_out, nand_5_out);
  nand nand_5 (nand_5_out, nand_4_out, not_1_out, nand_2_out);
  nand nand_6 (nand_6_out, nand_3_out, nand_4_out);
  nand nand_7 (nand_7_out, nand_5_out, nand_3_out);
  nand nand_8 (Q, nand_6_out, QBar);
  nand nand_9 (QBar, Q, not_1_out, nand_7_out);

  // Notes on the sheet:
  //   Maskter Slave JK Flip Flop
endmodule
