// Logisim project Registers.circ as structural Verilog: 3 circuits, main circuit Bit8_Register
module Bit8_Register (
  input  I0,
  input  I4,
  input  I1,
  input  I5,
  input  I2,
  input  I6,
  input  I3,
  input  I7,
  input  Load,
  input  CP,
  input  Reset,
  output A0,
  output A4,
  output A1,
  output A5,
  output A2,
  output A6,
  output A3,
  output A7
);

  // Bit4_Register_Parallel_Load bit4_register_parallel_load_1: pin names not known; wires that end beside it: I0, I1, I2, I3, Load, CP, Reset, A0, A1, A2, A3
  // Bit4_Register_Parallel_Load bit4_register_parallel_load_2: pin names not known; wires that end beside it: I4, I5, I6, I7, Load, CP, Reset, A4, A5, A6, A7
endmodule

module Bit12_Register (
  input  I0,
  input  I4,
  input  I8,
  input  I1,
  input  I5,
  input  I9,
  input  I2,
  input  I6,
  input  I10,
  input  I3,
  input  I7,
  input  I11,
  input  Load,
  input  CP,
  input  Reset,
  output A0,
  output A4,
  output A8,
  output A1,
  output A5,
  output A9,
  output A2,
  output A6,
  output A10,
  output A3,
  output A7,
  output A11
);

  // Bit4_Register_Parallel_Load bit4_register_parallel_load_1: pin names not known; wires that end beside it: I0, I1, I2, I3, Load, CP, Reset, A0, A1, A2, A3
  // Bit4_Register_Parallel_Load bit4_register_parallel_load_2: pin names not known; wires that end beside it: I4, I5, I6, I7, Load, CP, Reset, A4, A5, A6, A7
  // Bit4_Register_Parallel_Load bit4_register_parallel_load_3: pin names not known; wires that end beside it: I8, I9, I10, I11, Load, CP, Reset, A8, A9, A10, A11
endmodule

module Bit16_Register (
  input  I0,
  input  I4,
  input  I8,
  input  I12,
  input  I1,
  input  I5,
  input  I9,
  input  I13,
  input  I2,
  input  I6,
  input  I10,
  input  I14,
  input  I3,
  input  I7,
  input  I11,
  input  I15,
  input  Load,
  input  CP,
  input  Reset,
  output A0,
  output A4,
  output A8,
  output A12,
  output A1,
  output A5,
  output A9,
  output A13,
  output A2,
  output A6,
  output A10,
  output A14,
  output A3,
  output A7,
  output A11,
  output A15
);

  // Bit4_Register_Parallel_Load bit4_register_parallel_load_1: pin names not known; wires that end beside it: I0, I1, I2, I3, Load, CP, Reset, A0, A1, A2, A3
  // Bit4_Register_Parallel_Load bit4_register_parallel_load_2: pin names not known; wires that end beside it: I4, I5, I6, I7, Load, CP, Reset, A4, A5, A6, A7
  // Bit4_Register_Parallel_Load bit4_register_parallel_load_3: pin names not known; wires that end beside it: I8, I9, I10, I11, Load, CP, Reset, A8, A9, A10, A11
  // Bit4_Register_Parallel_Load bit4_register_parallel_load_4: pin names not known; wires that end beside it: I12, I13, I14, I15, Load, CP, Reset, A12, A13, A14, A15
endmodule
