// Logisim project ALSU.circ as structural Verilog: 5 circuits, main circuit Bit16_ALSU
module Bit16_ALSU (
  input  [15:0] A,
  input  [15:0] B,
  input  [3:0] S,
  input  C_prev,
  output [15:0] F,
  output C_next
);

  wire shiftleft_1_o_next, shiftleft_2_o_next, shiftright_1_o_prev;
  wire [15:0] and_1_out, and_2_out, and_3_out, and_4_out, bit16_arithmetic_unit_1_c_next,
       bit16_arithmetic_unit_1_d, bit16_logic_unit_1_yi, bit_extender_1_out, bit_extender_2_out, not_1_out,
       not_2_out, shiftleft_1_o, shiftleft_2_o, shiftright_1_o;

  ShiftLeft shiftleft_1 (
    .I_prev(C_prev), .I(bit16_arithmetic_unit_1_c_next), .O(shiftleft_1_o), .O_next(shiftleft_1_o_next));
  ShiftLeft shiftleft_2 (.I_prev(C_prev), .I(A), .O(shiftleft_2_o), .O_next(shiftleft_2_o_next));
  ShiftRight shiftright_1 (.I(A), .I_next(C_prev), .O_prev(shiftright_1_o_prev), .O(shiftright_1_o));
  Bit16_Arithmetic_Unit bit16_arithmetic_unit_1 (
    .A(A), .B(B), .S0(S[0]), .S1(S[1]), .C_prev(shiftleft_1_o), .C_next(bit16_arithmetic_unit_1_c_next),
    .D(bit16_arithmetic_unit_1_d));
  Bit16_Logic_Unit bit16_logic_unit_1 (.A(A), .B(B), .S0(S[0]), .S1(S[1]), .Yi(bit16_logic_unit_1_yi));
  Mux4x1 mux4x1_1 (
    .I0(shiftleft_1_o_next), .I1(1'b0), .I2(shiftleft_2_o_next), .I3(shiftright_1_o_prev), .S1(S[3]),
    .S0(S[2]), .Y(C_next));
  assign not_1_out = ~bit_extender_1_out;  // NOT_Gate not_1, 16 bits wide
  assign bit_extender_1_out = {{15{S[2]}}, S[2]};  // Bit_Extender bit_extender_1
  assign bit_extender_2_out = {{15{S[3]}}, S[3]};  // Bit_Extender bit_extender_2
  assign not_2_out = ~bit_extender_2_out;  // NOT_Gate not_2, 16 bits wide
  assign and_1_out = bit16_arithmetic_unit_1_d & not_1_out & not_2_out;  // AND_Gate and_1, 16 bits wide
  assign and_2_out = bit16_logic_unit_1_yi & bit_extender_1_out & not_2_out;  // AND_Gate and_2, 16 bits wide
  assign and_3_out = shiftleft_2_o & not_1_out & bit_extender_2_out;  // AND_Gate and_3, 16 bits wide
  assign and_4_out = shiftright_1_o & bit_extender_1_out & bit_extender_2_out;  // AND_Gate and_4, 16 bits wide
  assign F = and_1_out | and_2_out | and_3_out | and_4_out;  // OR_Gate or_1, 16 bits wide

  // Notes on the sheet:
  //   A_prev
  //   A_next
  //   C_prev
  //   ALSU For Moris Mano Machine
  //   ALSU is just a combinational circuit that performs all the provided operations, and the one required is chosen.
  //   Mux 4x1 couldn't be imported here.
endmodule

module ShiftRight (
  input  [15:0] I,
  input  I_next,
  output O_prev,
  output [15:0] O
);


  assign O = {I_next, I[15:1]};
  assign O_prev = I[0];
endmodule

module ShiftLeft (
  input  I_prev,
  input  [15:0] I,
  output [15:0] O,
  output O_next
);


  assign O = {I[14:0], I_prev};
  assign O_next = I[15];
endmodule

module Bit16_Logic_Unit (
  input  [15:0] A,
  input  [15:0] B,
  input  S0,
  input  S1,
  output [15:0] Yi
);

  wire [15:0] and_1_out, not_1_out, or_1_out, xor_1_out;

  assign and_1_out = A & B;  // AND_Gate and_1, 16 bits wide
  assign or_1_out = A | B;  // OR_Gate or_1, 16 bits wide
  assign xor_1_out = A ^ B;  // XOR_Gate xor_1, 16 bits wide
  assign not_1_out = ~A;  // NOT_Gate not_1, 16 bits wide
  Bit16Mux4x1 bit16mux4x1_1 (
    .I0(and_1_out), .I1(or_1_out), .I2(xor_1_out), .I3(not_1_out), .S0(S0), .S1(S1), .out_7(Yi));
endmodule

module Bit16_Arithmetic_Unit (
  input  [15:0] A,
  input  [15:0] B,
  input  S0,
  input  S1,
  input  [15:0] C_prev,
  output [15:0] C_next,
  output [15:0] D
);

  wire [15:0] bit16mux4x1_1_out_7, not_1_out;

  assign not_1_out = ~B;  // NOT_Gate not_1, 16 bits wide
  Bit16Mux4x1 bit16mux4x1_1 (
    .I0(B), .I1(not_1_out), .I2({16{1'b0}}), .I3({16{1'b1}}), .S0(S0), .S1(S1), .out_7(bit16mux4x1_1_out_7));
  Bit16_Full_Adder bit16_full_adder_1 (.P(A), .Q(bit16mux4x1_1_out_7), .R(C_prev), .C(C_next), .S(D));

  // Notes on the sheet:
  //   Di = Ai + Yi + Ci
endmodule
