// Logisim project Arithmetic_Unit.circ as structural Verilog: 1 circuit, main circuit Bit16_Arithmatic_Unit
module Bit16_Arithmatic_Unit (
  input  [15:0] A,
  input  [15:0] B,
  input  S0,
  input  S1,
  input  [15:0] C_prev,
  output [15:0] C_next,
  output [15:0] D
);

  wire [15:0] bit16mux4x1_1_out_7, not_1_out;

  assign not_1_out = ~B;  // NOT_Gate not_1, 16 bits wide
  Bit16Mux4x1 bit16mux4x1_1 (
    .I0(B), .I1(not_1_out), .I2({16{1'b0}}), .I3({16{1'b1}}), .S0(S0), .S1(S1), .out_7(bit16mux4x1_1_out_7));
  Bit16_Full_Adder bit16_full_adder_1 (.P(A), .Q(bit16mux4x1_1_out_7), .R(C_prev), .C(C_next), .S(D));

  // Notes on the sheet:
  //   Di = Ai + Yi + Ci
endmodule
