// Logisim project Logic_Unit.circ as structural Verilog: 1 circuit, main circuit Bit1_Logic_Unit
module Bit1_Logic_Unit (
  input  Ai,
  input  Bi,
  input  S1,
  input  S0,
  output Yi
);

  wire and_1_out, not_1_out, or_1_out, xor_1_out;

  and and_1 (and_1_out, Ai, Bi);
  or or_1 (or_1_out, Ai, Bi);
  xor xor_1 (xor_1_out, Ai, Bi);
  not not_1 (not_1_out, Ai);
  Mux4x1 mux4x1_1 (.I0(and_1_out), .I1(or_1_out), .I2(xor_1_out), .I3(not_1_out), .S1(S1), .S0(S0), .Y(Yi));
endmodule
