// Logisim project ALU_Control.circ as structural Verilog: 1 circuit, main circuit ALSU_ControlUnit
module ALSU_ControlUnit (
  input  B7,
  input  B6,
  input  D0,
  input  B9,
  input  D2,
  input  T5,
  input  r,
  input  p,
  input  B11,
  output [3:0] S
);

  wire and_1_out, and_2_out, and_3_out, and_4_out, and_5_out, and_6_out, and_7_out, and_8_out;

  and and_1 (and_1_out, r, B7);
  and and_2 (and_2_out, r, B6);
  and and_3 (and_3_out, D0, T5);
  and and_4 (and_4_out, r, B9);
  and and_5 (and_5_out, r, B7);
  and and_6 (and_6_out, r, B9);
  and and_7 (and_7_out, D2, T5);
  and and_8 (and_8_out, p, B11);
  or or_1 (S[3], and_1_out, and_2_out);
  or or_2 (S[2], and_3_out, and_4_out, and_5_out);
  and and_9 (S[0], r, B9);
  or or_3 (S[1], and_6_out, and_8_out, and_7_out);
endmodule
