// Logisim project AR.circ as structural Verilog: 1 circuit, main circuit AR_ControlUnit
module AR_ControlUnit (
  input  D7,
  input  I,
  input  T3,
  input  T2,
  input  R,
  input  T0,
  input  D5,
  input  T4,
  input  CLR,
  output ARLD,
  output ARINR,
  output ARCLR
);

  wire and_1_out, and_2_out, and_3_out, and_5_out, not_1_out, not_2_out;

  not not_1 (not_1_out, D7);
  not not_2 (not_2_out, R);
  and and_1 (and_1_out, not_1_out, I, T3);
  and and_2 (and_2_out, T2, not_2_out);
  and and_3 (and_3_out, not_2_out, T0);
  and and_4 (ARINR, D5, T4);
  and and_5 (and_5_out, T0, R);
  or or_1 (ARLD, and_1_out, and_2_out, and_3_out);
  or or_2 (ARCLR, and_5_out, CLR);

  // Notes on the sheet:
  //   Load = R'T0+R'T2+D'7IT3
  //   Increment = D5T4 (BSA)
  //   Clear = RT0
endmodule
