// Logisim project IR.circ as structural Verilog: 1 circuit, main circuit IR_ControlUnit
module IR_ControlUnit (
  input  R,
  input  T1,
  input  CLR,
  output IRLD,
  output IRCLR
);

  and and_1 (IRLD, R, T1);

  assign IRCLR = CLR;
endmodule
