// Logisim project PC.circ as structural Verilog: 1 circuit, main circuit PC_ControlUnit
module PC_ControlUnit (
  input  D4,
  input  T4,
  input  D5,
  input  T5,
  input  R,
  input  T1,
  input  in_7,
  input  B11,
  input  B9,
  input  B5,
  input  CLR,
  output PCLD,
  output PCINR,
  output PCCLR
);

  wire and_1_out, and_2_out, and_3_out, and_4_out, and_5_out, and_6_out, and_7_out, not_1_out;

  not not_1 (not_1_out, R);
  and and_1 (and_1_out, D4, T4);
  and and_2 (and_2_out, D5, T5);
  and and_3 (and_3_out, not_1_out, T1);
  and and_4 (and_4_out, in_7, B11);
  and and_5 (and_5_out, in_7, B9);
  and and_6 (and_6_out, in_7, B5);
  and and_7 (and_7_out, R, T1);
  or or_1 (PCLD, and_1_out, and_2_out);
  or or_2 (PCINR, and_3_out, and_4_out, and_5_out, and_6_out);
  or or_3 (PCCLR, and_7_out, CLR);

  // Notes on the sheet:
  //   Load = D4T4 + D5T5
  //   BUN & BSA
  //   Fetch & Skip Instructions
  //   Increment = R'T1 + rB11 + rB9 + rB5
  //   Clear = RT1
endmodule
